# Fritzing sketch Planta_Twittera (saved by Fritzing 0.9.3b)
breadboards: 1

parts:
  U1 = NodeMCU V1.0
  DHT1 = DHT11 Humitidy and Temperature Sensor
  Componente1 = Soil Moisture Sensor
  R1 = Resistor [tolerance=±5% resistance=10k package=THT]

nets:
  N1: U1.D4, DHT1.DATA, R1.Pin_1
  3V3: U1.3V3, DHT1.VDD, Componente1.VCC, R1.Pin_0
  GND: U1.GND, DHT1.GND, Componente1.GND
  N2: U1.A0, Componente1.SIG

custom parts:
  NodeMCU V1.0: ESP8266 based NodeMCU
  DHT11 Humitidy and Temperature Sensor: DHT11 Humidity and Temperature Sensor
